# Fritzing sketch ESP32 Arduino with DHT11 Sensor (saved by Fritzing 0.9.3b)
breadboards: 1

parts:
  M1 = DOIT Esp32 DevKit v1 (30 pins long, 11 pins width) [part_number=ESP32S-PIN30]
  DHT1 = DHT11 Humitidy and Temperature Sensor
  R1 = Resistor [tolerance=±5% resistance=220 package=THT]

nets:
  3V3: M1.3V3, DHT1.VDD, R1.Pin_1
  GND: M1.GND, DHT1.GND
  N1: M1.D15, DHT1.DATA, R1.Pin_0

notes:
  TheCustomizeWindows.COM

custom parts:
  DOIT Esp32 DevKit v1 (30 pins long, 11 pins width): The DOIT Esp32 DevKit v1 is one of the development board created by DOIT to evaluate the ESP-WROOM-32 module. It is based on the ESP32 microcontroller that boasts Wifi, Bluetooth, Ethernet and Low Power support all in a single chip. (vanepp) made breadboard work, adjusted pin numbering and labels and reduced size of schematic and cleaned up pcb. This chip is 30pins long (2 x15) and 11 pins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
  DHT11 Humitidy and Temperature Sensor: DHT11 Humidity and Temperature Sensor
